// Logisim project alu-control.circ as structural Verilog: 1 circuit, main circuit main
module main (
  input  [5:0] Instruction_5_0,
  input  [3:0] ALUOp,
  output [3:0] ALUSwitch,
  output isJR,
  output IsShift
);

  wire _0, _1, _2, _5, _6, _9, _10, _14, _15, comparator_10_eq, comparator_11_eq, isRType, not_1_out,
       not_2_out, not_3_out, not_4_out, or_1_out, or_2_out, or_3_out, or_4_out, or_5_out, or_6_out, or_7_out;
  wire [3:0] multiplexer_1_out, multiplexer_2_out, multiplexer_3_out, multiplexer_4_out, multiplexer_5_out,
       multiplexer_6_out, multiplexer_7_out, multiplexer_8_out, multiplexer_9_out;

  Comparator #(.width(6)) comparator_1 (.a(Instruction_5_0), .b({6{1'b0}}), .eq(_0));  // open: gt, lt
  Comparator #(.width(6)) comparator_2 (.a(Instruction_5_0), .b(6'b000010), .eq(_1));  // open: gt, lt
  Comparator #(.width(6)) comparator_3 (.a(Instruction_5_0), .b(6'b000011), .eq(_2));  // open: gt, lt
  Comparator #(.width(6)) comparator_4 (.a(Instruction_5_0), .b(6'b100000), .eq(_5));  // open: gt, lt
  Comparator #(.width(6)) comparator_5 (.a(Instruction_5_0), .b(6'b100001), .eq(_6));  // open: gt, lt
  Comparator #(.width(6)) comparator_6 (.a(Instruction_5_0), .b(6'b101010), .eq(_14));  // open: gt, lt
  Comparator #(.width(6)) comparator_7 (.a(Instruction_5_0), .b(6'b101011), .eq(_15));  // open: gt, lt
  Comparator #(.width(6)) comparator_8 (.a(Instruction_5_0), .b(6'b100100), .eq(_9));  // open: gt, lt
  Comparator #(.width(6)) comparator_9 (.a(Instruction_5_0), .b(6'b100101), .eq(_10));  // open: gt, lt
  Comparator #(.width(6)) comparator_10 (.a(Instruction_5_0), .b(6'b001000), .eq(comparator_10_eq));  // open: gt, lt
  and and_1 (isJR, isRType, comparator_10_eq);
  Multiplexer #(.width(4), .enable("false")) multiplexer_1 (
    .in0(4'b0001), .in1(4'b0000), .out(multiplexer_1_out), .sel(_0));
  Multiplexer #(.width(4), .enable("false")) multiplexer_2 (
    .in0(4'b0101), .in1(4'b0010), .out(multiplexer_2_out), .sel(_2));
  Multiplexer #(.width(4), .enable("false")) multiplexer_3 (
    .in0(4'b1110), .in1(4'b0110), .out(multiplexer_3_out), .sel(_6));
  Multiplexer #(.width(4), .enable("false")) multiplexer_4 (
    .in0(4'b1001), .in1(4'b1111), .out(multiplexer_4_out), .sel(_15));
  Multiplexer #(.width(4), .enable("false")) multiplexer_5 (
    .in0(multiplexer_1_out), .in1(multiplexer_2_out), .out(multiplexer_5_out), .sel(not_1_out));
  not not_1 (not_1_out, or_1_out);
  or or_1 (or_1_out, _0, _1);
  Multiplexer #(.width(4), .enable("false")) multiplexer_6 (
    .in0(multiplexer_3_out), .in1(multiplexer_4_out), .out(multiplexer_6_out), .sel(not_2_out));
  not not_2 (not_2_out, or_2_out);
  or or_2 (or_2_out, _6, _14);
  or or_3 (or_3_out, or_1_out, _2, _5);
  or or_4 (or_4_out, or_2_out, _15, _9);
  or or_5 (or_5_out, _0, _1, _2);
  Multiplexer #(.width(4), .enable("false")) multiplexer_7 (
    .in0(multiplexer_5_out), .in1(multiplexer_6_out), .out(multiplexer_7_out), .sel(not_3_out));
  not not_3 (not_3_out, or_3_out);
  and and_2 (IsShift, isRType, or_5_out);
  not not_4 (not_4_out, or_6_out);
  or or_6 (or_6_out, or_3_out, or_4_out);
  Multiplexer #(.width(4), .enable("false")) multiplexer_8 (
    .in0(multiplexer_7_out), .in1(4'b1010), .out(multiplexer_8_out), .sel(not_4_out));
  or or_7 (or_7_out, ALUOp[3], ALUOp[2], ALUOp[1], ALUOp[0]);
  Comparator #(.width(4)) comparator_11 (.a(ALUOp), .b(4'b0001), .eq(comparator_11_eq));  // open: gt, lt
  Multiplexer #(.width(4), .enable("false")) multiplexer_9 (
    .in0(multiplexer_8_out), .in1(ALUOp), .out(multiplexer_9_out), .sel(or_7_out));
  not not_5 (isRType, or_7_out);
  Multiplexer #(.width(4), .enable("false")) multiplexer_10 (
    .in0(multiplexer_9_out), .in1(4'b0000), .out(ALUSwitch), .sel(comparator_11_eq));
endmodule
