// Logisim project alu.circ as structural Verilog: 7 circuits, main circuit main
module main (
  input  [31:0] X,
  input  [31:0] Y,
  input  [3:0] Switch,
  output Signed_Overflow,
  output Equal,
  output [31:0] Result
);

  wire and_2_out, and_3_out, and_4_out, and_5_out, and_6_out, comparator_1_lt, comparator_2_lt, not_1_out,
       not_2_out, not_3_out, not_4_out, not_5_out, not_6_out, OF_minus, or_2_out;
  wire [31:0] ADD, AND, OR, SLL, SLT, SLTU, SRA, SRL, SUB;

  Comparator #(.width(32)) comparator_1 (.a(X), .b(Y), .lt(comparator_1_lt));  // open: gt, eq
  Comparator #(.width(32), .mode("unsigned")) comparator_2 (.a(X), .b(Y), .lt(comparator_2_lt));  // open: gt, eq
  Shifter #(.width(32)) shifter_1 (.in(Y), .\dist (X[4:0]), .out(SLL));
  Shifter #(.width(32), .shift("lr")) shifter_2 (.in(Y), .\dist (X[4:0]), .out(SRL));
  Shifter #(.width(32), .shift("ar")) shifter_3 (.in(Y), .\dist (X[4:0]), .out(SRA));
  assign SLT = {{31{1'b0}}, comparator_1_lt};  // Bit_Extender bit_extender_1
  assign SLTU = {{31{1'b0}}, comparator_2_lt};  // Bit_Extender bit_extender_2
  Adder #(.width(32)) adder_1 (.a(X), .b(Y), .out(ADD));  // open: cin, cout
  Subtractor #(.width(32)) subtractor_1 (.a(X), .b(Y), .out(SUB), .bout(OF_minus));  // open: bin
  assign AND = X & Y;  // AND_Gate and_1, 32 bits wide
  assign OR = X | Y;  // OR_Gate or_1, 32 bits wide
  Multiplexer #(.select(4), .width(32), .enable("false")) multiplexer_1 (
    .in0(SLL), .in1(SRL), .in2(SRA), .in5(ADD), .in6(ADD), .in7(SUB), .in8(SUB), .in9(AND), .in10(OR),
    .in14(SLT), .in15(SLTU), .out(Result), .sel(Switch));  // open: in3, in4, in11, in12, in13
  not not_1 (not_1_out, ADD[31]);
  not not_2 (not_2_out, X[31]);
  not not_3 (not_3_out, Y[31]);
  not not_4 (not_4_out, Switch[3]);
  not not_5 (not_5_out, Switch[1]);
  and and_2 (and_2_out, X[31], Y[31], not_1_out);
  and and_3 (and_3_out, not_2_out, ADD[31], not_3_out);
  not not_6 (not_6_out, Switch[3]);
  and and_4 (and_4_out, not_4_out, Switch[2], not_5_out, Switch[0]);
  or or_2 (or_2_out, and_2_out, and_3_out);
  and and_5 (and_5_out, not_6_out, Switch[2], OF_minus, Switch[1], Switch[0]);
  and and_6 (and_6_out, and_4_out, or_2_out);
  isEqual isEqual (.X(X), .Y(Y), .isEqual(Equal));
  or or_3 (Signed_Overflow, and_6_out, and_5_out);

  // Other names for the same wires on the sheet: ADDU[31:0] = ADD; overflow = Signed_Overflow; S[3:0] = Switch;
  //   SUBU[31:0] = SUB

  // Notes on the sheet:
  //   INPUTS to your circuit
  //   SHIFTING
  //   LESS THAN
  //   DON'T CHANGE THE LOCATIONS OF THE INPUTS AND OUTPUTS!
  //   OPERANDS AND LOGIC
  //   OUTPUTS from your circuit
  //   OVERFLOW AND EQUAL
endmodule

module isEqual (
  input  [31:0] X,
  input  [31:0] Y,
  output isEqual
);

  wire or_1_out;
  wire [31:0] xor_1_out;

  assign xor_1_out = X ^ Y;  // XOR_Gate xor_1, 32 bits wide
  or or_1 (or_1_out, xor_1_out[0], xor_1_out[1], xor_1_out[2], xor_1_out[3], xor_1_out[4], xor_1_out[5], xor_1_out[6], xor_1_out[7], xor_1_out[8], xor_1_out[9], xor_1_out[10], xor_1_out[11], xor_1_out[12], xor_1_out[13], xor_1_out[14], xor_1_out[15], xor_1_out[17], xor_1_out[18], xor_1_out[19], xor_1_out[20], xor_1_out[21], xor_1_out[22], xor_1_out[23], xor_1_out[24], xor_1_out[25], xor_1_out[26], xor_1_out[27], xor_1_out[28], xor_1_out[29], xor_1_out[30], xor_1_out[31], xor_1_out[16]);
  not not_1 (isEqual, or_1_out);
endmodule

module leftShift1 (
  input  arithmetic,
  input  [31:0] Y,
  output [31:0] out
);

  and and_1 (out[0], arithmetic, Y[0]);

  assign out[31:1] = Y[30:0];
endmodule

module rightShift1 (
  input  [31:0] Y,
  input  arithmetic,
  output [31:0] out
);

  and and_1 (out[31], Y[31], arithmetic);

  assign out[30:0] = Y[31:1];
endmodule

module _0SLL (
  input  arithmetic,
  input  [31:0] Y___Input,
  input  [31:0] X___shmnt,
  output [31:0] Y__X
);

  wire and_1_out, and_2_out, and_3_out, and_4_out, and_5_out, or_1_out, or_2_out, or_3_out, or_4_out,
       or_5_out, or_7_out, X_32;
  wire [31:0] leftshift1_1_out, leftshift1_2_out, leftshift1_3_out, leftshift1_4_out, leftshift1_5_out,
       leftshift1_6_out, leftshift1_7_out, leftshift1_8_out, leftshift1_9_out, leftshift1_10_out,
       leftshift1_11_out, leftshift1_12_out, leftshift1_13_out, leftshift1_14_out, leftshift1_15_out,
       leftshift1_16_out, leftshift1_17_out, leftshift1_18_out, leftshift1_19_out, leftshift1_20_out,
       leftshift1_21_out, leftshift1_22_out, leftshift1_23_out, leftshift1_24_out, leftshift1_25_out,
       leftshift1_26_out, leftshift1_27_out, leftshift1_28_out, leftshift1_29_out, leftshift1_30_out,
       leftshift1_31_out, leftshift1_32_out, multiplexer_1_out, multiplexer_2_out, multiplexer_3_out,
       multiplexer_4_out, multiplexer_5_out;

  leftShift1 leftshift1_1 (.Y(Y___Input), .arithmetic(arithmetic), .out(leftshift1_1_out));
  Multiplexer #(.width(32), .enable("false")) multiplexer_1 (
    .in0(Y___Input), .in1(leftshift1_1_out), .out(multiplexer_1_out), .sel(or_1_out));
  or or_1 (or_1_out, X___shmnt[0], X_32);
  and and_1 (and_1_out, X___shmnt[0], X___shmnt[5]);
  leftShift1 leftshift1_2 (.Y(multiplexer_1_out), .arithmetic(arithmetic), .out(leftshift1_2_out));
  leftShift1 leftshift1_3 (.Y(leftshift1_2_out), .arithmetic(arithmetic), .out(leftshift1_3_out));
  and and_2 (and_2_out, X___shmnt[1], X___shmnt[5]);
  and and_3 (and_3_out, X___shmnt[2], X___shmnt[5]);
  Multiplexer #(.width(32), .enable("false")) multiplexer_2 (
    .in0(multiplexer_1_out), .in1(leftshift1_3_out), .out(multiplexer_2_out), .sel(or_2_out));
  or or_2 (or_2_out, X_32, X___shmnt[1]);
  and and_4 (and_4_out, X___shmnt[3], X___shmnt[5]);
  leftShift1 leftshift1_4 (.Y(multiplexer_2_out), .arithmetic(arithmetic), .out(leftshift1_4_out));
  leftShift1 leftshift1_5 (.Y(leftshift1_4_out), .arithmetic(arithmetic), .out(leftshift1_5_out));
  and and_5 (and_5_out, X___shmnt[4], X___shmnt[5]);
  leftShift1 leftshift1_6 (.Y(leftshift1_7_out), .arithmetic(arithmetic), .out(leftshift1_6_out));
  leftShift1 leftshift1_7 (.Y(leftshift1_5_out), .arithmetic(arithmetic), .out(leftshift1_7_out));
  or or_3 (or_3_out, and_1_out, and_2_out, and_3_out, and_4_out, and_5_out);
  Multiplexer #(.width(32), .enable("false")) multiplexer_3 (
    .in0(multiplexer_2_out), .in1(leftshift1_6_out), .out(multiplexer_3_out), .sel(or_4_out));
  leftShift1 leftshift1_8 (.Y(multiplexer_3_out), .arithmetic(arithmetic), .out(leftshift1_8_out));
  leftShift1 leftshift1_9 (.Y(leftshift1_8_out), .arithmetic(arithmetic), .out(leftshift1_9_out));
  leftShift1 leftshift1_10 (.Y(leftshift1_9_out), .arithmetic(arithmetic), .out(leftshift1_10_out));
  leftShift1 leftshift1_11 (.Y(leftshift1_10_out), .arithmetic(arithmetic), .out(leftshift1_11_out));
  or or_4 (or_4_out, X___shmnt[2], X_32);
  leftShift1 leftshift1_12 (.Y(leftshift1_13_out), .arithmetic(arithmetic), .out(leftshift1_12_out));
  leftShift1 leftshift1_13 (.Y(leftshift1_14_out), .arithmetic(arithmetic), .out(leftshift1_13_out));
  leftShift1 leftshift1_14 (.Y(leftshift1_15_out), .arithmetic(arithmetic), .out(leftshift1_14_out));
  leftShift1 leftshift1_15 (.Y(leftshift1_11_out), .arithmetic(arithmetic), .out(leftshift1_15_out));
  Multiplexer #(.width(32), .enable("false")) multiplexer_4 (
    .in0(multiplexer_3_out), .in1(leftshift1_12_out), .out(multiplexer_4_out), .sel(or_5_out));
  leftShift1 leftshift1_16 (.Y(multiplexer_4_out), .arithmetic(arithmetic), .out(leftshift1_16_out));
  leftShift1 leftshift1_17 (.Y(leftshift1_16_out), .arithmetic(arithmetic), .out(leftshift1_17_out));
  leftShift1 leftshift1_18 (.Y(leftshift1_17_out), .arithmetic(arithmetic), .out(leftshift1_18_out));
  leftShift1 leftshift1_19 (.Y(leftshift1_18_out), .arithmetic(arithmetic), .out(leftshift1_19_out));
  or or_5 (or_5_out, X_32, X___shmnt[3]);
  leftShift1 leftshift1_20 (.Y(leftshift1_19_out), .arithmetic(arithmetic), .out(leftshift1_20_out));
  leftShift1 leftshift1_21 (.Y(leftshift1_20_out), .arithmetic(arithmetic), .out(leftshift1_21_out));
  leftShift1 leftshift1_22 (.Y(leftshift1_21_out), .arithmetic(arithmetic), .out(leftshift1_22_out));
  leftShift1 leftshift1_23 (.Y(leftshift1_22_out), .arithmetic(arithmetic), .out(leftshift1_23_out));
  or or_6 (X_32, or_3_out, X___shmnt[6], X___shmnt[7], X___shmnt[8], X___shmnt[9], X___shmnt[10], X___shmnt[11], X___shmnt[12], X___shmnt[13], X___shmnt[14], X___shmnt[15], X___shmnt[16], X___shmnt[17], X___shmnt[18], X___shmnt[19], X___shmnt[20], X___shmnt[21], X___shmnt[22], X___shmnt[23], X___shmnt[24], X___shmnt[25], X___shmnt[26], X___shmnt[27], X___shmnt[28], X___shmnt[29], X___shmnt[30], X___shmnt[31]);
  leftShift1 leftshift1_24 (.Y(leftshift1_25_out), .arithmetic(arithmetic), .out(leftshift1_24_out));
  leftShift1 leftshift1_25 (.Y(leftshift1_26_out), .arithmetic(arithmetic), .out(leftshift1_25_out));
  leftShift1 leftshift1_26 (.Y(leftshift1_27_out), .arithmetic(arithmetic), .out(leftshift1_26_out));
  leftShift1 leftshift1_27 (.Y(leftshift1_28_out), .arithmetic(arithmetic), .out(leftshift1_27_out));
  leftShift1 leftshift1_28 (.Y(leftshift1_29_out), .arithmetic(arithmetic), .out(leftshift1_28_out));
  leftShift1 leftshift1_29 (.Y(leftshift1_30_out), .arithmetic(arithmetic), .out(leftshift1_29_out));
  leftShift1 leftshift1_30 (.Y(leftshift1_31_out), .arithmetic(arithmetic), .out(leftshift1_30_out));
  leftShift1 leftshift1_31 (.Y(leftshift1_23_out), .arithmetic(arithmetic), .out(leftshift1_31_out));
  Multiplexer #(.width(32), .enable("false")) multiplexer_5 (
    .in0(multiplexer_4_out), .in1(leftshift1_24_out), .out(multiplexer_5_out), .sel(or_7_out));
  or or_7 (or_7_out, X___shmnt[4], X_32);
  Multiplexer #(.width(32), .enable("false")) multiplexer_6 (
    .in0(multiplexer_5_out), .in1(leftshift1_32_out), .out(Y__X), .sel(X_32));
  leftShift1 leftshift1_32 (.Y(multiplexer_5_out), .arithmetic(arithmetic), .out(leftshift1_32_out));
endmodule

module _1_2SR (
  input  arithmetic,
  input  [31:0] Y___Input,
  input  [31:0] X___shmnt,
  output [31:0] Y__X
);

  wire and_1_out, and_2_out, and_3_out, and_4_out, and_5_out, or_1_out, or_2_out, or_3_out, or_4_out,
       or_5_out, or_7_out, X_32;
  wire [31:0] multiplexer_1_out, multiplexer_2_out, multiplexer_3_out, multiplexer_4_out, multiplexer_5_out,
       rightshift1_1_out, rightshift1_2_out, rightshift1_3_out, rightshift1_4_out, rightshift1_5_out,
       rightshift1_6_out, rightshift1_7_out, rightshift1_8_out, rightshift1_9_out, rightshift1_10_out,
       rightshift1_11_out, rightshift1_12_out, rightshift1_13_out, rightshift1_14_out, rightshift1_15_out,
       rightshift1_16_out, rightshift1_17_out, rightshift1_18_out, rightshift1_19_out, rightshift1_20_out,
       rightshift1_21_out, rightshift1_22_out, rightshift1_23_out, rightshift1_24_out, rightshift1_25_out,
       rightshift1_26_out, rightshift1_27_out, rightshift1_28_out, rightshift1_29_out, rightshift1_30_out,
       rightshift1_31_out, rightshift1_32_out;

  rightShift1 rightshift1_1 (.Y(Y___Input), .arithmetic(arithmetic), .out(rightshift1_1_out));
  Multiplexer #(.width(32), .enable("false")) multiplexer_1 (
    .in0(Y___Input), .in1(rightshift1_1_out), .out(multiplexer_1_out), .sel(or_1_out));
  or or_1 (or_1_out, X___shmnt[0], X_32);
  and and_1 (and_1_out, X___shmnt[0], X___shmnt[5]);
  rightShift1 rightshift1_2 (.Y(multiplexer_1_out), .arithmetic(arithmetic), .out(rightshift1_2_out));
  rightShift1 rightshift1_3 (.Y(rightshift1_2_out), .arithmetic(arithmetic), .out(rightshift1_3_out));
  and and_2 (and_2_out, X___shmnt[1], X___shmnt[5]);
  and and_3 (and_3_out, X___shmnt[2], X___shmnt[5]);
  Multiplexer #(.width(32), .enable("false")) multiplexer_2 (
    .in0(multiplexer_1_out), .in1(rightshift1_3_out), .out(multiplexer_2_out), .sel(or_2_out));
  or or_2 (or_2_out, X_32, X___shmnt[1]);
  and and_4 (and_4_out, X___shmnt[3], X___shmnt[5]);
  rightShift1 rightshift1_4 (.Y(multiplexer_2_out), .arithmetic(arithmetic), .out(rightshift1_4_out));
  rightShift1 rightshift1_5 (.Y(rightshift1_4_out), .arithmetic(arithmetic), .out(rightshift1_5_out));
  and and_5 (and_5_out, X___shmnt[4], X___shmnt[5]);
  rightShift1 rightshift1_6 (.Y(rightshift1_5_out), .arithmetic(arithmetic), .out(rightshift1_6_out));
  rightShift1 rightshift1_7 (.Y(rightshift1_6_out), .arithmetic(arithmetic), .out(rightshift1_7_out));
  or or_3 (or_3_out, and_1_out, and_2_out, and_3_out, and_4_out, and_5_out);
  Multiplexer #(.width(32), .enable("false")) multiplexer_3 (
    .in0(multiplexer_2_out), .in1(rightshift1_7_out), .out(multiplexer_3_out), .sel(or_4_out));
  rightShift1 rightshift1_8 (.Y(multiplexer_3_out), .arithmetic(arithmetic), .out(rightshift1_8_out));
  rightShift1 rightshift1_9 (.Y(rightshift1_8_out), .arithmetic(arithmetic), .out(rightshift1_9_out));
  rightShift1 rightshift1_10 (.Y(rightshift1_9_out), .arithmetic(arithmetic), .out(rightshift1_10_out));
  rightShift1 rightshift1_11 (.Y(rightshift1_10_out), .arithmetic(arithmetic), .out(rightshift1_11_out));
  or or_4 (or_4_out, X___shmnt[2], X_32);
  rightShift1 rightshift1_12 (.Y(rightshift1_13_out), .arithmetic(arithmetic), .out(rightshift1_12_out));
  rightShift1 rightshift1_13 (.Y(rightshift1_14_out), .arithmetic(arithmetic), .out(rightshift1_13_out));
  rightShift1 rightshift1_14 (.Y(rightshift1_15_out), .arithmetic(arithmetic), .out(rightshift1_14_out));
  rightShift1 rightshift1_15 (.Y(rightshift1_11_out), .arithmetic(arithmetic), .out(rightshift1_15_out));
  Multiplexer #(.width(32), .enable("false")) multiplexer_4 (
    .in0(multiplexer_3_out), .in1(rightshift1_12_out), .out(multiplexer_4_out), .sel(or_5_out));
  or or_5 (or_5_out, X_32, X___shmnt[3]);
  or or_6 (X_32, or_3_out, X___shmnt[6], X___shmnt[7], X___shmnt[8], X___shmnt[9], X___shmnt[10], X___shmnt[11], X___shmnt[12], X___shmnt[13], X___shmnt[14], X___shmnt[15], X___shmnt[16], X___shmnt[17], X___shmnt[18], X___shmnt[19], X___shmnt[20], X___shmnt[21], X___shmnt[22], X___shmnt[23], X___shmnt[24], X___shmnt[25], X___shmnt[26], X___shmnt[27], X___shmnt[28], X___shmnt[29], X___shmnt[30], X___shmnt[31]);
  rightShift1 rightshift1_16 (.Y(rightshift1_18_out), .arithmetic(arithmetic), .out(rightshift1_16_out));
  rightShift1 rightshift1_17 (.Y(multiplexer_4_out), .arithmetic(arithmetic), .out(rightshift1_17_out));
  rightShift1 rightshift1_18 (.Y(rightshift1_20_out), .arithmetic(arithmetic), .out(rightshift1_18_out));
  rightShift1 rightshift1_19 (.Y(rightshift1_17_out), .arithmetic(arithmetic), .out(rightshift1_19_out));
  rightShift1 rightshift1_20 (.Y(rightshift1_22_out), .arithmetic(arithmetic), .out(rightshift1_20_out));
  rightShift1 rightshift1_21 (.Y(rightshift1_19_out), .arithmetic(arithmetic), .out(rightshift1_21_out));
  rightShift1 rightshift1_22 (.Y(rightshift1_24_out), .arithmetic(arithmetic), .out(rightshift1_22_out));
  rightShift1 rightshift1_23 (.Y(rightshift1_21_out), .arithmetic(arithmetic), .out(rightshift1_23_out));
  rightShift1 rightshift1_24 (.Y(rightshift1_26_out), .arithmetic(arithmetic), .out(rightshift1_24_out));
  rightShift1 rightshift1_25 (.Y(rightshift1_23_out), .arithmetic(arithmetic), .out(rightshift1_25_out));
  rightShift1 rightshift1_26 (.Y(rightshift1_28_out), .arithmetic(arithmetic), .out(rightshift1_26_out));
  rightShift1 rightshift1_27 (.Y(rightshift1_25_out), .arithmetic(arithmetic), .out(rightshift1_27_out));
  rightShift1 rightshift1_28 (.Y(rightshift1_30_out), .arithmetic(arithmetic), .out(rightshift1_28_out));
  rightShift1 rightshift1_29 (.Y(rightshift1_27_out), .arithmetic(arithmetic), .out(rightshift1_29_out));
  rightShift1 rightshift1_30 (.Y(rightshift1_31_out), .arithmetic(arithmetic), .out(rightshift1_30_out));
  rightShift1 rightshift1_31 (.Y(rightshift1_29_out), .arithmetic(arithmetic), .out(rightshift1_31_out));
  Multiplexer #(.width(32), .enable("false")) multiplexer_5 (
    .in0(multiplexer_4_out), .in1(rightshift1_16_out), .out(multiplexer_5_out), .sel(or_7_out));
  or or_7 (or_7_out, X___shmnt[4], X_32);
  rightShift1 rightshift1_32 (.Y(multiplexer_5_out), .arithmetic(arithmetic), .out(rightshift1_32_out));
  Multiplexer #(.width(32), .enable("false")) multiplexer_6 (
    .in0(multiplexer_5_out), .in1(rightshift1_32_out), .out(Y__X), .sel(X_32));
endmodule

module shamtConverter (
  input  [31:0] in_1
);
endmodule
