// Logisim project cpu-sc.circ as structural Verilog: 1 circuit, main circuit main
module main (
  input  [31:0] INSTRUCTION,
  input  CLOCK,
  output [31:0] FETCH_ADDRESS,
  output [31:0] s0_Value,
  output [31:0] s1_Value,
  output [31:0] s2_Value,
  output [31:0] ra_Value,
  output [31:0] sp_Value,
  output [3:0] swinc
);

  wire BEQ_out, BLTZALTrue, BNE_out, comparator_1_lt, Control_alusrc, Control_beq, Control_bltzal,
       Control_bne, Control_jal, Control_jump, Control_memtoreg, Control_memwrite, Control_regwrite, isJR,
       main_2_equal, nor_1_out, not_2_out, or_1_out, Save__ra_out, xor_1_out;
  wire [1:0] Control_regdst;
  wire [3:0] ALU_Control_aluswitch;
  wire [4:0] multiplexer_1_out;
  wire [31:0] adder_2_out, bit_extender_1_out, JRAddress, main_1_read_data_2, main_2_result, main_3_p5,
       multiplexer_2_out, multiplexer_3_out, multiplexer_4_out, multiplexer_5_out, multiplexer_6_out,
       multiplexer_7_out, PC_4, shifter_1_out;

  Register #(.width(32)) PC (.D(multiplexer_6_out), .Q(FETCH_ADDRESS), .clk(CLOCK));  // open: en, clr
  Adder #(.width(32)) adder_1 (.a(FETCH_ADDRESS), .b(32'h4), .out(PC_4));  // open: cin, cout
  // NOT_Gate not_1 is placed but not wired
  xor xor_1 (xor_1_out, isJR, Control_regwrite);
  Multiplexer #(.select(2), .width(5), .enable("false")) multiplexer_1 (
    .in0(INSTRUCTION[20:16]), .in1(INSTRUCTION[15:11]), .in2({5{1'b1}}), .out(multiplexer_1_out),
    .sel(Control_regdst));  // open: in3
  control_main Control (
    .instruction_31_26(INSTRUCTION[31:26]), .RegDst(Control_regdst), .Jump(Control_jump), .BNE(Control_bne),
    .BEQ(Control_beq), .MemtoReg(Control_memtoreg), .ALUOp(swinc), .MemWrite(Control_memwrite),
    .ALUSrc(Control_alusrc), .RegWrite(Control_regwrite), .JAL(Control_jal), .BLTZAL(Control_bltzal));
  assign bit_extender_1_out = {{16{INSTRUCTION[15]}}, INSTRUCTION[15:0]};  // Bit_Extender bit_extender_1
  regfile_main main_1 (
    .Read_Register_1(INSTRUCTION[25:21]), .Read_Register_2(INSTRUCTION[20:16]),
    .Write_Register(multiplexer_1_out), .Write_Data(multiplexer_2_out), .Write_Enable(xor_1_out),
    .Clock(CLOCK), .Read_Data_1(JRAddress), .Read_Data_2(main_1_read_data_2), .s0_Value(s0_Value),
    .s1_Value(s1_Value), .s2_Value(s2_Value), .ra_Value(ra_Value), .sp_Value(sp_Value));
  Multiplexer #(.width(32), .enable("false")) multiplexer_2 (
    .in0(multiplexer_7_out), .in1(PC_4), .out(multiplexer_2_out), .sel(Save__ra_out));
  Multiplexer #(.width(32)) multiplexer_3 (
    .in0({PC_4[31:28], INSTRUCTION[25:0], 2'b00}), .in1(JRAddress), .out(multiplexer_3_out), .sel(isJR));  // open: en
  or Save__ra (Save__ra_out, Control_jal, BLTZALTrue);
  Shifter #(.width(32)) shifter_1 (.in(bit_extender_1_out), .\dist (5'b00010), .out(shifter_1_out));
  Multiplexer #(.width(32), .enable("false")) multiplexer_4 (
    .in0(main_1_read_data_2), .in1(bit_extender_1_out), .out(multiplexer_4_out), .sel(Control_alusrc));
  alu_control_main ALU_Control (
    .Instruction_5_0(INSTRUCTION[5:0]), .ALUOp(swinc), .ALUSwitch(ALU_Control_aluswitch), .isJR(isJR));
  Adder #(.width(32)) adder_2 (.a(PC_4), .b(shifter_1_out), .out(adder_2_out));  // open: cin, cout
  not not_2 (not_2_out, main_2_equal);
  alu_main main_2 (
    .Switch(ALU_Control_aluswitch), .X(JRAddress), .Equal(main_2_equal), .Result(main_2_result),
    .Y(multiplexer_4_out));  // open: Signed_Overflow
  Multiplexer #(.width(32), .enable("false")) multiplexer_5 (
    .in0(PC_4), .in1(adder_2_out), .out(multiplexer_5_out), .sel(or_1_out));
  or or_1 (or_1_out, BNE_out, BEQ_out, BLTZALTrue);
  and BEQ (BEQ_out, main_2_equal, Control_beq);
  and BNE (BNE_out, Control_bne, not_2_out);
  Comparator #(.width(32)) comparator_1 (.a(main_2_result), .b({32{1'b0}}), .lt(comparator_1_lt));  // open: gt, eq
  Multiplexer #(.width(32), .enable("false")) multiplexer_6 (
    .in0(multiplexer_3_out), .in1(multiplexer_5_out), .out(multiplexer_6_out), .sel(nor_1_out));
  nor nor_1 (nor_1_out, Control_jump, isJR);
  and BLTZAL (BLTZALTrue, Control_bltzal, comparator_1_lt);
  // mem_main main_3: pin names not known; wires that end beside it: main_2_result, main_1_read_data_2, Control_memwrite, CLOCK, main_3_p5
  Multiplexer #(.width(32), .enable("false")) multiplexer_7 (
    .in0(main_3_p5), .in1(main_2_result), .out(multiplexer_7_out), .sel(Control_memtoreg));

  // Other names for the same wires on the sheet: clk = CLOCK; fetch_addr[31:0] = FETCH_ADDRESS; ra[31:0] = ra_Value;
  //   s0[31:0] = s0_Value; s1[31:0] = s1_Value; s2[31:0] = s2_Value; sp[31:0] = sp_Value

  // Notes on the sheet:
  //   Output
  //   PC + 4
  //   PIPELINE GOES HERE
  //   For JAL, $ra
  //   These are outputs/inputs from run.circ
  //   Inputs
  //   Jump Address
  //   These are DEBUG/TEST outputs from your circuit.
  //   PCSource
endmodule
