// Logisim project cpu.circ as structural Verilog: 1 circuit, main circuit main
module main (
  input  [31:0] INSTRUCTION,
  input  CLOCK,
  output [31:0] FETCH_ADDRESS,
  output [31:0] s0_Value,
  output [31:0] s1_Value,
  output [31:0] s2_Value,
  output [31:0] ra_Value,
  output [31:0] sp_Value,
  output [3:0] ALUOP
);

  wire BEQ_out, BLTZALTrue, BNE_out, comparator_1_lt, Control_alusrc, Control_beq, Control_bltzal,
       Control_bne, Control_jal, Control_jump, Control_memtoreg, Control_memwrite, Control_regwrite, isJR,
       isLUI, isShift, main_2_equal, NOOP, nor_1_out, not_1_out, or_1_out, or_2_out, Save__ra_out, xor_1_out;
  wire [1:0] Control_regdst;
  wire [3:0] ALU_Control_aluswitch;
  wire [4:0] multiplexer_2_out;
  wire [31:0] adder_2_out, bit_extender_1_out, JR_Address, main_1_read_data_2, main_2_result, main_3_p5,
       multiplexer_1_out, multiplexer_3_out, multiplexer_4_out, multiplexer_5_out, multiplexer_6_out,
       multiplexer_7_out, multiplexer_8_out, multiplexer_9_out, multiplexer_10_out, PC_4, register_1_q,
       register_2_q, SHAMT, shifter_1_out;

  Register #(.width(32)) PC (.D(multiplexer_9_out), .Q(FETCH_ADDRESS), .clk(CLOCK));  // open: en, clr
  Adder #(.width(32)) adder_1 (.a(FETCH_ADDRESS), .b(32'h4), .out(PC_4));  // open: cin, cout
  Register #(.width(32)) register_1 (.D(PC_4), .Q(register_1_q), .clk(CLOCK));  // open: en, clr
  Multiplexer #(.width(32)) multiplexer_1 (
    .in0(INSTRUCTION), .in1({32{1'b0}}), .out(multiplexer_1_out), .sel(NOOP));  // open: en
  Register #(.width(32)) register_2 (.D(multiplexer_1_out), .Q(register_2_q), .clk(CLOCK));  // open: en, clr
  // Probe on register_2_q[10:6]
  xor xor_1 (xor_1_out, isJR, Control_regwrite);
  Multiplexer #(.select(2), .width(5), .enable("false")) multiplexer_2 (
    .in0(register_2_q[20:16]), .in1(register_2_q[15:11]), .in2({5{1'b1}}), .out(multiplexer_2_out),
    .sel(Control_regdst));  // open: in3
  assign bit_extender_1_out = {{16{register_2_q[15]}}, register_2_q[15:0]};  // Bit_Extender bit_extender_1
  assign SHAMT = {{27{1'b0}}, register_2_q[10:6]};  // Bit_Extender bit_extender_2
  control_main Control (
    .instruction_31_26(register_2_q[31:26]), .RegDst(Control_regdst), .Jump(Control_jump), .BNE(Control_bne),
    .BEQ(Control_beq), .MemtoReg(Control_memtoreg), .ALUOp(ALUOP), .MemWrite(Control_memwrite),
    .ALUSrc(Control_alusrc), .RegWrite(Control_regwrite), .JAL(Control_jal), .BLTZAL(Control_bltzal),
    .isLUI(isLUI));
  or or_1 (or_1_out, xor_1_out, BLTZALTrue);
  regfile_main main_1 (
    .Read_Register_1(register_2_q[25:21]), .Read_Register_2(register_2_q[20:16]),
    .Write_Register(multiplexer_2_out), .Write_Data(multiplexer_3_out), .Write_Enable(or_1_out),
    .Clock(CLOCK), .Read_Data_1(JR_Address), .Read_Data_2(main_1_read_data_2), .s0_Value(s0_Value),
    .s1_Value(s1_Value), .s2_Value(s2_Value), .ra_Value(ra_Value), .sp_Value(sp_Value));
  or Save__ra (Save__ra_out, Control_jal, BLTZALTrue);
  Multiplexer #(.width(32), .enable("false")) multiplexer_3 (
    .in0(multiplexer_10_out), .in1(FETCH_ADDRESS), .out(multiplexer_3_out), .sel(Save__ra_out));
  alu_control_main ALU_Control (
    .Instruction_5_0(register_2_q[5:0]), .ALUOp(ALUOP), .ALUSwitch(ALU_Control_aluswitch), .isJR(isJR),
    .IsShift(isShift));
  Multiplexer #(.width(32)) multiplexer_4 (
    .in0({register_1_q[31:28], register_2_q[25:0], 2'b00}), .in1(JR_Address), .out(multiplexer_4_out),
    .sel(isJR));  // open: en
  Shifter #(.width(32)) shifter_1 (.in(bit_extender_1_out), .\dist (5'b00010), .out(shifter_1_out));
  Multiplexer #(.width(32)) multiplexer_5 (
    .in0(JR_Address), .in1(SHAMT), .out(multiplexer_5_out), .sel(isShift));  // open: en
  Multiplexer #(.width(32), .enable("false")) multiplexer_6 (
    .in0(main_1_read_data_2), .in1(bit_extender_1_out), .out(multiplexer_6_out), .sel(Control_alusrc));
  Adder #(.width(32)) adder_2 (.a(register_1_q), .b(shifter_1_out), .out(adder_2_out));  // open: cin, cout
  // Probe on multiplexer_6_out
  Multiplexer #(.width(32)) multiplexer_7 (
    .in0(multiplexer_5_out), .in1(32'hf), .out(multiplexer_7_out), .sel(isLUI));  // open: en
  or or_2 (or_2_out, BNE_out, BEQ_out, BLTZALTrue);
  and BNE (BNE_out, Control_bne, not_1_out);
  not not_1 (not_1_out, main_2_equal);
  alu_main main_2 (
    .Switch(ALU_Control_aluswitch), .X(multiplexer_7_out), .Equal(main_2_equal), .Result(main_2_result),
    .Y(multiplexer_6_out));  // open: Signed_Overflow
  Multiplexer #(.width(32), .enable("false")) multiplexer_8 (
    .in0(PC_4), .in1(adder_2_out), .out(multiplexer_8_out), .sel(or_2_out));
  and BLTZAL (BLTZALTrue, Control_bltzal, comparator_1_lt);
  and BEQ (BEQ_out, main_2_equal, Control_beq);
  Comparator #(.width(32)) comparator_1 (.a(main_2_result), .b({32{1'b0}}), .lt(comparator_1_lt));  // open: gt, eq
  Multiplexer #(.width(32), .enable("false")) multiplexer_9 (
    .in0(multiplexer_4_out), .in1(multiplexer_8_out), .out(multiplexer_9_out), .sel(nor_1_out));
  nor nor_1 (nor_1_out, isJR, Control_jump);
  or or_3 (NOOP, or_2_out, isJR, Control_jump);
  // mem_main main_3: pin names not known; wires that end beside it: main_2_result, main_1_read_data_2, Control_memwrite, CLOCK, main_3_p5
  Multiplexer #(.width(32), .enable("false")) multiplexer_10 (
    .in0(main_3_p5), .in1(main_2_result), .out(multiplexer_10_out), .sel(Control_memtoreg));

  // Other names for the same wires on the sheet: clk = CLOCK; fetch_addr[31:0] = FETCH_ADDRESS;
  //   PC[31:0] = FETCH_ADDRESS; ra[31:0] = ra_Value; s0[31:0] = s0_Value; s1[31:0] = s1_Value; s2[31:0] = s2_Value;
  //   sp[31:0] = sp_Value

  // Notes on the sheet:
  //   Output
  //   PC + 4
  //   For JAL, $ra
  //   These are outputs/inputs from run.circ
  //   PIPELINE
  //   PIPELINE
  //   Inputs
  //   Jump Address
  //   These are DEBUG/TEST outputs from your circuit.
  //   PCSource
endmodule
