// Logisim project regfile.circ as structural Verilog: 3 circuits, main circuit main
module main (
  input  [4:0] Read_Register_1,
  input  [4:0] Read_Register_2,
  input  [4:0] Write_Register,
  input  [31:0] Write_Data,
  input  Write_Enable,
  input  Clock,
  output [31:0] s0_Value,
  output [31:0] s1_Value,
  output [31:0] s2_Value,
  output [31:0] ra_Value,
  output [31:0] sp_Value,
  output [31:0] Read_Data_1,
  output [31:0] Read_Data_2
);

  wire demultiplexer_1_out0, demultiplexer_1_out1, demultiplexer_1_out2, demultiplexer_1_out3;
  wire [31:0] reggroup0_1_readreg1, reggroup0_1_readreg2, reggroup_1_readreg1, reggroup_1_readreg2,
       reggroup_2_readreg1, reggroup_2_readreg2, reggroup_3_readreg1, reggroup_3_readreg2;

  Demultiplexer #(.select(2)) demultiplexer_1 (
    .out0(demultiplexer_1_out0), .out1(demultiplexer_1_out1), .out2(demultiplexer_1_out2),
    .out3(demultiplexer_1_out3), .in(Write_Enable), .sel(Write_Register[4:3]));  // open: en
  reggroup0 reggroup0_1 (
    .toWrite(Write_Data), .Enable(demultiplexer_1_out0), .WriteSelect(Write_Register[2:0]), .rclk(Clock),
    .ReadSelect1(Write_Register[2:0]), .ReadSelect2(Read_Register_2[2:0]), .ReadReg1(reggroup0_1_readreg1),
    .ReadReg2(reggroup0_1_readreg2));  // open: DebugSelect1, DebugOut1, DebugSelect2, out_11, DebugSelect3, out_12
  reggroup reggroup_1 (
    .toWrite(Write_Data), .Enable(demultiplexer_1_out2), .DebugSelect1(3'b000), .DebugOut1(s0_Value),
    .DebugSelect2(3'b001), .out_11(s1_Value), .DebugSelect3(3'b010), .out_12(s2_Value),
    .WriteSelect(Write_Register[2:0]), .rclk(Clock), .ReadSelect1(Read_Register_1[2:0]),
    .ReadSelect2(Read_Register_2[2:0]), .ReadReg1(reggroup_1_readreg1), .ReadReg2(reggroup_1_readreg2));
  reggroup reggroup_2 (
    .toWrite(Write_Data), .Enable(demultiplexer_1_out1), .WriteSelect(Write_Register[2:0]), .rclk(Clock),
    .ReadSelect1(Read_Register_1[2:0]), .ReadSelect2(Read_Register_2[2:0]), .ReadReg1(reggroup_2_readreg1),
    .ReadReg2(reggroup_2_readreg2));  // open: DebugSelect1, DebugOut1, DebugSelect2, out_11, DebugSelect3, out_12
  reggroup reggroup_3 (
    .toWrite(Write_Data), .Enable(demultiplexer_1_out3), .DebugSelect1(3'b111), .DebugOut1(ra_Value),
    .DebugSelect2(3'b101), .out_11(sp_Value), .WriteSelect(Write_Register[2:0]), .rclk(Clock),
    .ReadSelect1(Read_Register_1[2:0]), .ReadSelect2(Read_Register_2[2:0]), .ReadReg1(reggroup_3_readreg1),
    .ReadReg2(reggroup_3_readreg2));  // open: DebugSelect3, out_12
  Multiplexer #(.select(2), .width(32)) multiplexer_1 (
    .in0(reggroup0_1_readreg1), .in1(reggroup_2_readreg1), .in2(reggroup_1_readreg1),
    .in3(reggroup_3_readreg1), .out(Read_Data_1), .sel(Read_Register_1[4:3]));  // open: en
  Multiplexer #(.select(2), .width(32)) multiplexer_2 (
    .in0(reggroup0_1_readreg2), .in1(reggroup_2_readreg2), .in2(reggroup_1_readreg2),
    .in3(reggroup_3_readreg2), .out(Read_Data_2), .sel(Read_Register_2[4:3]));  // open: en

  // Other names for the same wires on the sheet: clk = Clock; ra[31:0] = ra_Value; read_data1[31:0] = Read_Data_1;
  //   read_data2[31:0] = Read_Data_2; read_reg1[4:0] = Read_Register_1; read_reg2[4:0] = Read_Register_2;
  //   s0[31:0] = s0_Value; s1[31:0] = s1_Value; s2[31:0] = s2_Value; sp[31:0] = sp_Value; write_en = Write_Enable;
  //   write_reg[4:0] = Write_Register

  // Notes on the sheet:
  //   INPUTS to your circuit
  //   DON'T CHANGE THE LOCATIONS OF THE INPUTS AND OUTPUTS!
  //   These are DEBUG/TEST outputs from your circuit.
  //   OUTPUTS from your circuit
endmodule

module reggroup (
  input  [2:0] DebugSelect1,
  input  [2:0] DebugSelect2,
  input  [2:0] DebugSelect3,
  input  [31:0] toWrite,
  input  Enable,
  input  [2:0] WriteSelect,
  input  [2:0] ReadSelect1,
  input  [2:0] ReadSelect2,
  input  rclk,
  output [31:0] DebugOut1,
  output [31:0] out_11,
  output [31:0] out_12,
  output [31:0] ReadReg1,
  output [31:0] ReadReg2
);

  wire demultiplexer_1_out0, demultiplexer_1_out1, demultiplexer_1_out2, demultiplexer_1_out3,
       demultiplexer_1_out4, demultiplexer_1_out5, demultiplexer_1_out6, demultiplexer_1_out7;
  wire [31:0] register_1_q, register_2_q, register_3_q, register_4_q, register_5_q, register_6_q,
       register_7_q, register_8_q;

  Demultiplexer #(.select(3)) demultiplexer_1 (
    .out0(demultiplexer_1_out0), .out1(demultiplexer_1_out1), .out2(demultiplexer_1_out2),
    .out3(demultiplexer_1_out3), .out4(demultiplexer_1_out4), .out5(demultiplexer_1_out5),
    .out6(demultiplexer_1_out6), .out7(demultiplexer_1_out7), .in(Enable), .sel(WriteSelect));  // open: en
  Multiplexer #(.select(3), .width(32)) multiplexer_1 (
    .in0(register_1_q), .in1(register_3_q), .in2(register_5_q), .in3(register_7_q), .in4(register_2_q),
    .in5(register_4_q), .in6(register_6_q), .in7(register_8_q), .out(DebugOut1), .sel(DebugSelect1));  // open: en
  Register #(.width(32)) register_1 (
    .D(toWrite), .en(demultiplexer_1_out0), .Q(register_1_q), .clk(rclk));  // open: clr
  Register #(.width(32)) register_2 (
    .D(toWrite), .en(demultiplexer_1_out4), .Q(register_2_q), .clk(rclk));  // open: clr
  Multiplexer #(.select(3), .width(32)) multiplexer_2 (
    .in0(register_1_q), .in1(register_3_q), .in2(register_5_q), .in3(register_7_q), .in4(register_2_q),
    .in5(register_4_q), .in6(register_6_q), .in7(register_8_q), .out(out_11), .sel(DebugSelect2));  // open: en
  Register #(.width(32)) register_3 (
    .D(toWrite), .en(demultiplexer_1_out1), .Q(register_3_q), .clk(rclk));  // open: clr
  Register #(.width(32)) register_4 (
    .D(toWrite), .en(demultiplexer_1_out5), .Q(register_4_q), .clk(rclk));  // open: clr
  Register #(.width(32)) register_5 (
    .D(toWrite), .en(demultiplexer_1_out2), .Q(register_5_q), .clk(rclk));  // open: clr
  Register #(.width(32)) register_6 (
    .D(toWrite), .en(demultiplexer_1_out6), .Q(register_6_q), .clk(rclk));  // open: clr
  Register #(.width(32)) register_7 (
    .D(toWrite), .en(demultiplexer_1_out3), .Q(register_7_q), .clk(rclk));  // open: clr
  Register #(.width(32)) register_8 (
    .D(toWrite), .en(demultiplexer_1_out7), .Q(register_8_q), .clk(rclk));  // open: clr
  Multiplexer #(.select(3), .width(32)) multiplexer_3 (
    .in0(register_1_q), .in1(register_3_q), .in2(register_5_q), .in3(register_7_q), .in4(register_2_q),
    .in5(register_4_q), .in6(register_6_q), .in7(register_8_q), .out(out_12), .sel(DebugSelect3));  // open: en
  Multiplexer #(.select(3), .width(32)) multiplexer_4 (
    .in0(register_1_q), .in1(register_3_q), .in2(register_5_q), .in3(register_7_q), .in4(register_2_q),
    .in5(register_4_q), .in6(register_6_q), .in7(register_8_q), .out(ReadReg1), .sel(ReadSelect1));  // open: en
  Multiplexer #(.select(3), .width(32)) multiplexer_5 (
    .in0(register_1_q), .in1(register_3_q), .in2(register_5_q), .in3(register_7_q), .in4(register_2_q),
    .in5(register_4_q), .in6(register_6_q), .in7(register_8_q), .out(ReadReg2), .sel(ReadSelect2));  // open: en
endmodule

module reggroup0 (
  input  [2:0] DebugSelect1,
  input  [2:0] DebugSelect2,
  input  [2:0] DebugSelect3,
  input  [31:0] toWrite,
  input  Enable,
  input  [2:0] WriteSelect,
  input  [2:0] ReadSelect1,
  input  [2:0] ReadSelect2,
  input  rclk,
  output [31:0] DebugOut1,
  output [31:0] out_11,
  output [31:0] out_12,
  output [31:0] ReadReg1,
  output [31:0] ReadReg2
);

  wire demultiplexer_1_out1, demultiplexer_1_out2, demultiplexer_1_out3, demultiplexer_1_out4,
       demultiplexer_1_out5, demultiplexer_1_out6, demultiplexer_1_out7;
  wire [31:0] register_1_q, register_2_q, register_3_q, register_4_q, register_5_q, register_6_q,
       register_7_q, register_8_q;

  Demultiplexer #(.select(3)) demultiplexer_1 (
    .out1(demultiplexer_1_out1), .out2(demultiplexer_1_out2), .out3(demultiplexer_1_out3),
    .out4(demultiplexer_1_out4), .out5(demultiplexer_1_out5), .out6(demultiplexer_1_out6),
    .out7(demultiplexer_1_out7), .in(Enable), .sel(WriteSelect));  // open: out0, en
  Multiplexer #(.select(3), .width(32)) multiplexer_1 (
    .in0(register_1_q), .in1(register_3_q), .in2(register_5_q), .in3(register_7_q), .in4(register_2_q),
    .in5(register_4_q), .in6(register_6_q), .in7(register_8_q), .out(DebugOut1), .sel(DebugSelect1));  // open: en
  Register #(.width(32)) register_1 (.D(toWrite), .en(1'b0), .Q(register_1_q), .clk(rclk));  // open: clr
  Register #(.width(32)) register_2 (
    .D(toWrite), .en(demultiplexer_1_out4), .Q(register_2_q), .clk(rclk));  // open: clr
  Multiplexer #(.select(3), .width(32)) multiplexer_2 (
    .in0(register_1_q), .in1(register_3_q), .in2(register_5_q), .in3(register_7_q), .in4(register_2_q),
    .in5(register_4_q), .in6(register_6_q), .in7(register_8_q), .out(out_11), .sel(DebugSelect2));  // open: en
  Register #(.width(32)) register_3 (
    .D(toWrite), .en(demultiplexer_1_out1), .Q(register_3_q), .clk(rclk));  // open: clr
  Register #(.width(32)) register_4 (
    .D(toWrite), .en(demultiplexer_1_out5), .Q(register_4_q), .clk(rclk));  // open: clr
  Register #(.width(32)) register_5 (
    .D(toWrite), .en(demultiplexer_1_out2), .Q(register_5_q), .clk(rclk));  // open: clr
  Register #(.width(32)) register_6 (
    .D(toWrite), .en(demultiplexer_1_out6), .Q(register_6_q), .clk(rclk));  // open: clr
  Register #(.width(32)) register_7 (
    .D(toWrite), .en(demultiplexer_1_out3), .Q(register_7_q), .clk(rclk));  // open: clr
  Register #(.width(32)) register_8 (
    .D(toWrite), .en(demultiplexer_1_out7), .Q(register_8_q), .clk(rclk));  // open: clr
  Multiplexer #(.select(3), .width(32)) multiplexer_3 (
    .in0(register_1_q), .in1(register_3_q), .in2(register_5_q), .in3(register_7_q), .in4(register_2_q),
    .in5(register_4_q), .in6(register_6_q), .in7(register_8_q), .out(out_12), .sel(DebugSelect3));  // open: en
  Multiplexer #(.select(3), .width(32)) multiplexer_4 (
    .in0(register_1_q), .in1(register_3_q), .in2(register_5_q), .in3(register_7_q), .in4(register_2_q),
    .in5(register_4_q), .in6(register_6_q), .in7(register_8_q), .out(ReadReg1), .sel(ReadSelect1));  // open: en
  Multiplexer #(.select(3), .width(32)) multiplexer_5 (
    .in0(register_1_q), .in1(register_3_q), .in2(register_5_q), .in3(register_7_q), .in4(register_2_q),
    .in5(register_4_q), .in6(register_6_q), .in7(register_8_q), .out(ReadReg2), .sel(ReadSelect2));  // open: en
endmodule
